// Logisim project Adder.circ as structural Verilog: 1 circuit, main circuit main
module main (
  input  ADD_SUB,
  input  B3,
  input  B2,
  input  B1,
  input  B0,
  input  A3,
  input  A2,
  input  A1,
  input  A0,
  output CARRY,
  output X3,
  output X2,
  output X1,
  output X0
);

  wire and_1_out, and_2_out, and_3_out, and_4_out, and_5_out, and_6_out, and_7_out, and_8_out, or_1_out,
       or_2_out, or_3_out, xor_1_out, xor_2_out, xor_3_out, xor_4_out, xor_5_out, xor_6_out, xor_11_out,
       xor_12_out;

  xor xor_1 (xor_1_out, xor_5_out, A0);
  and and_1 (and_1_out, xor_5_out, A0);
  xor xor_2 (xor_2_out, xor_6_out, A1);
  and and_2 (and_2_out, xor_6_out, A1);
  xor xor_3 (xor_3_out, xor_11_out, A2);
  and and_3 (and_3_out, xor_11_out, A2);
  xor xor_4 (xor_4_out, xor_12_out, A3);
  and and_4 (and_4_out, xor_12_out, A3);
  xor xor_5 (xor_5_out, ADD_SUB, B0);
  and and_5 (and_5_out, ADD_SUB, xor_1_out);
  and and_6 (and_6_out, or_1_out, xor_2_out);
  and and_7 (and_7_out, or_2_out, xor_3_out);
  and and_8 (and_8_out, or_3_out, xor_4_out);
  xor xor_6 (xor_6_out, ADD_SUB, B1);
  xor xor_7 (X0, xor_1_out, ADD_SUB);
  or or_1 (or_1_out, and_5_out, and_1_out);
  xor xor_8 (X1, xor_2_out, or_1_out);
  or or_2 (or_2_out, and_6_out, and_2_out);
  xor xor_9 (X2, xor_3_out, or_2_out);
  or or_3 (or_3_out, and_7_out, and_3_out);
  xor xor_10 (X3, xor_4_out, or_3_out);
  or or_4 (CARRY, and_8_out, and_4_out);
  xor xor_11 (xor_11_out, ADD_SUB, B2);
  xor xor_12 (xor_12_out, ADD_SUB, B3);

  // Notes on the sheet:
  //   8    4    2    1
  //   8    4    2    1
  //   8    4    2    1
endmodule
